# Fritzing sketch epaper_wifi_temp (saved by Fritzing 0.8.7b)
breadboards: 1

parts:
  DHT1 = DHT11 Humitidy and Temperature Sensor
  A2 = Waveshare 1.54in epaper display
  A3 = Arduino Nano 33 BLE Sense

nets:
  N1: DHT1.VDD, A2.Pin_8, A3.Pin_2
  N2: DHT1.DATA, A3.Pin_20
  N3: DHT1.GND, A2.Pin_7, A3.Pin_14, A3.Pin_19
  N4: A2.Pin_1, A3.Pin_25
  N5: A2.Pin_2, A3.Pin_26
  N6: A2.Pin_3, A3.Pin_27
  N7: A2.Pin_4, A3.Pin_28
  N8: A2.Pin_5, A3.Pin_1
  N9: A2.Pin_6, A3.Pin_29
  N10: A3.Pin_13, A3.Pin_18

custom parts:
  DHT11 Humitidy and Temperature Sensor: DHT11 Humidity and Temperature Sensor
  Waveshare 1.54in epaper display: This is an E-Ink display module, 1.54inch, 200x200 resolution, with embedded controller, communicating via SPI interface.
  Arduino Nano 33 BLE Sense: The Nano 33 BLE Sense (without headers) is Arduino’s 3.3V AI enabled board in the smallest available form factor: 45x18mm! The Arduino Nano 33 BLE Sense is a completely new board on a well-known form factor. It comes with a series of embedded sensors: 9 axis inertial sensor: what makes this board ideal for wearable devices humidity, and temperature sensor: to get highly accurate measurements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
